// Logisim project hypercpu.circ as structural Verilog: 3 circuits, main circuit main
// Registers x16
module Registers (
  input  Clock,
  input  Reset,
  input  [31:0] Write_Data,
  input  [3:0] Write_Register,
  input  Write_Enable,
  input  [3:0] Read_A,
  input  [3:0] Read_B,
  input  [31:0] Write_Stack_Pointer,
  input  [31:0] Write_Program_Counter,
  output [31:0] Read_Data_A,
  output [31:0] Read_Data_B,
  output [31:0] Read_Stack_Pointer,
  output [31:0] Read_Program_Counter
);

  wire decoder_1_out0, decoder_1_out1, decoder_1_out2, decoder_1_out3, decoder_1_out4, decoder_1_out5,
       decoder_1_out6, decoder_1_out7, decoder_1_out8, decoder_1_out9, decoder_1_out10, decoder_1_out11,
       decoder_1_out12, decoder_1_out13, decoder_1_out14, decoder_1_out15;
  wire [31:0] multiplexer_1_out, multiplexer_2_out, multiplexer_3_out, multiplexer_4_out, r0_q, r1_q, r2_q,
       r3_q, r4_q, r5_q, r6_q, r7_q, r8_q, r9_q, ra_q, rb_q, rc_q, rd_q;

  Decoder #(.select(4), .disabled(0)) decoder_1 (
    .out0(decoder_1_out0), .out1(decoder_1_out1), .out2(decoder_1_out2), .out3(decoder_1_out3),
    .out4(decoder_1_out4), .out5(decoder_1_out5), .out6(decoder_1_out6), .out7(decoder_1_out7),
    .out8(decoder_1_out8), .out9(decoder_1_out9), .out10(decoder_1_out10), .out11(decoder_1_out11),
    .out12(decoder_1_out12), .out13(decoder_1_out13), .out14(decoder_1_out14), .out15(decoder_1_out15),
    .sel(Write_Register), .en(Write_Enable));
  Pull_Resistor pull_resistor_1 (.node(Write_Enable));
  Multiplexer #(.width(32), .enable("false")) multiplexer_1 (
    .in0(Write_Stack_Pointer), .in1(Write_Data), .out(multiplexer_1_out), .sel(decoder_1_out14));
  Multiplexer #(.width(32), .enable("false")) multiplexer_2 (
    .in0(Write_Program_Counter), .in1(Write_Data), .out(multiplexer_2_out), .sel(decoder_1_out15));
  Register #(.width(32), .trigger("falling")) r0 (
    .D(Write_Data), .en(decoder_1_out0), .Q(r0_q), .clk(Clock), .clr(Reset));
  Register #(.width(32), .trigger("falling")) r1 (
    .D(Write_Data), .en(decoder_1_out1), .Q(r1_q), .clk(Clock), .clr(Reset));
  Register #(.width(32), .trigger("falling")) r2 (
    .D(Write_Data), .en(decoder_1_out2), .Q(r2_q), .clk(Clock), .clr(Reset));
  Register #(.width(32), .trigger("falling")) r3 (
    .D(Write_Data), .en(decoder_1_out3), .Q(r3_q), .clk(Clock), .clr(Reset));
  Register #(.width(32), .trigger("falling")) r4 (
    .D(Write_Data), .en(decoder_1_out4), .Q(r4_q), .clk(Clock), .clr(Reset));
  Register #(.width(32), .trigger("falling")) r5 (
    .D(Write_Data), .en(decoder_1_out5), .Q(r5_q), .clk(Clock), .clr(Reset));
  Register #(.width(32), .trigger("falling")) r6 (
    .D(Write_Data), .en(decoder_1_out6), .Q(r6_q), .clk(Clock), .clr(Reset));
  Register #(.width(32), .trigger("falling")) r7 (
    .D(Write_Data), .en(decoder_1_out7), .Q(r7_q), .clk(Clock), .clr(Reset));
  Register #(.width(32), .trigger("falling")) r8 (
    .D(Write_Data), .en(decoder_1_out8), .Q(r8_q), .clk(Clock), .clr(Reset));
  Register #(.width(32), .trigger("falling")) r9 (
    .D(Write_Data), .en(decoder_1_out9), .Q(r9_q), .clk(Clock), .clr(Reset));
  Register #(.width(32), .trigger("falling")) ra (
    .D(Write_Data), .en(decoder_1_out10), .Q(ra_q), .clk(Clock), .clr(Reset));
  Register #(.width(32), .trigger("falling")) rb (
    .D(Write_Data), .en(decoder_1_out11), .Q(rb_q), .clk(Clock), .clr(Reset));
  Register #(.width(32), .trigger("falling")) rc (
    .D(Write_Data), .en(decoder_1_out12), .Q(rc_q), .clk(Clock), .clr(Reset));
  Register #(.width(32), .trigger("falling")) rd (
    .D(Write_Data), .en(decoder_1_out13), .Q(rd_q), .clk(Clock), .clr(Reset));
  Register #(.width(32), .trigger("falling")) sp (
    .D(multiplexer_1_out), .Q(Read_Stack_Pointer), .clk(Clock), .clr(Reset));  // open: en
  Register #(.width(32), .trigger("falling")) pc (
    .D(multiplexer_2_out), .Q(Read_Program_Counter), .clk(Clock), .clr(Reset));  // open: en
  Multiplexer #(.select(4), .width(32), .enable("false")) multiplexer_3 (
    .in0(r0_q), .in1(r1_q), .in2(r2_q), .in3(r3_q), .in4(r4_q), .in5(r5_q), .in6(r6_q), .in7(r7_q),
    .in8(r8_q), .in9(r9_q), .in10(ra_q), .in11(rb_q), .in12(rc_q), .in13(rd_q), .in14(Read_Stack_Pointer),
    .in15(Read_Program_Counter), .out(multiplexer_3_out), .sel(Read_A));
  Register #(.width(32)) register_1 (.D(multiplexer_3_out), .Q(Read_Data_A), .clk(Clock));  // open: en, clr
  Multiplexer #(.select(4), .width(32), .enable("false")) multiplexer_4 (
    .in0(r0_q), .in1(r1_q), .in2(r2_q), .in3(r3_q), .in4(r4_q), .in5(r5_q), .in6(r6_q), .in7(r7_q),
    .in8(r8_q), .in9(r9_q), .in10(ra_q), .in11(rb_q), .in12(rc_q), .in13(rd_q), .in14(Read_Stack_Pointer),
    .in15(Read_Program_Counter), .out(multiplexer_4_out), .sel(Read_B));
  Register #(.width(32)) register_2 (.D(multiplexer_4_out), .Q(Read_Data_B), .clk(Clock));  // open: en, clr
endmodule

module main (
  output [31:0] ALU_Result
);

  wire BR_out, comparator_1_eq, comparator_2_eq, comparator_3_eq, comparator_4_eq, comparator_5_eq,
       comparator_6_gt, comparator_7_eq, d_ff_1_q, MCLK, Memory_Write_Enable, not_1_out, Reset_out, toB_out,
       Write_Enable, xor_out;
  wire [3:0] register_1_q_2, register_1_q_3, register_1_q_4;
  wire [15:0] i;
  wire [31:0] A, adder_1_out, B, bit_extender_1_out, Memory_Address, Memory_Read, multiplexer_1_out, Next_PC,
       Next_SP, PC, register_1_q, register_3_q, SP, Write_Data;
  wire [31:16] Instruction;

  Comparator comparator_1 (.a(Memory_Address[31:24]), .b(8'h1), .eq(comparator_1_eq));  // open: gt, lt
  Hex_Digit_Display hex_digit_display_1 (.value(register_1_q[31:28]));  // open: dp
  Hex_Digit_Display hex_digit_display_2 (.value(register_1_q_4));  // open: dp
  Comparator comparator_2 (.a(Instruction[31:24]), .b(8'h2), .eq(comparator_2_eq));  // open: gt, lt
  Comparator comparator_3 (.a(Memory_Address[31:24]), .b({8{1'b0}}), .eq(comparator_3_eq));  // open: gt, lt
  Hex_Digit_Display hex_digit_display_3 (.value(register_1_q_3));  // open: dp
  Hex_Digit_Display hex_digit_display_4 (.value(register_1_q_2));  // open: dp
  Register #(.width(32), .trigger("falling")) register_1 (
    .D(A), .en(comparator_2_eq),
    .Q({register_1_q[31:28], register_1_q_4, register_1_q_3, register_1_q_2, register_1_q[15:0]}), .clk(MCLK));  // open: clr
  not not_1 (not_1_out, MCLK);
  Hex_Digit_Display hex_digit_display_5 (.value(register_1_q[11:8]));  // open: dp
  Hex_Digit_Display hex_digit_display_6 (.value(register_1_q[15:12]));  // open: dp
  ROM #(.addrWidth(24), .dataWidth(32)) rom_1 (.addr(Memory_Address[23:0]), .data(Memory_Read), .sel(comparator_3_eq));
  RAM #(.addrWidth(24), .dataWidth(32), .bus("separate")) ram_1 (
    .addr(Memory_Address[23:0]), .din(B), .data(Memory_Read), .str(Memory_Write_Enable),
    .sel(comparator_1_eq), .clk(not_1_out));  // open: ld, clr
  Hex_Digit_Display hex_digit_display_7 (.value(register_1_q[7:4]));  // open: dp
  Hex_Digit_Display hex_digit_display_8 (.value(register_1_q[3:0]));  // open: dp
  Clock clock_1 (.out(MCLK));
  Registers Registers (
    .Write_Data(Write_Data), .Read_A(Instruction[23:20]), .Read_Data_A(A), .Write_Program_Counter(Next_PC),
    .Write_Register(Instruction[19:16]), .Write_Enable(Write_Enable), .Read_Program_Counter(PC),
    .Reset(d_ff_1_q), .Clock(MCLK), .Read_B(Instruction[19:16]), .Read_Data_B(B),
    .Write_Stack_Pointer(Next_SP), .Read_Stack_Pointer(SP));
  Button Reset (.out(Reset_out));
  D_Flip_Flop #(.trigger("falling")) d_ff_1 (
    .clk(MCLK), .D(1'b0), .Q(d_ff_1_q), .preset(Reset_out));  // open: Qn, en, reset
  Multiplexer #(.width(32), .enable("false")) multiplexer_1 (
    .in0(B), .in1(bit_extender_1_out), .out(multiplexer_1_out), .sel(Instruction[28]));
  assign bit_extender_1_out = {{16{i[15]}}, i};  // Bit_Extender bit_extender_1
  ALU ALU (.A(A), .B(multiplexer_1_out), .R(ALU_Result), .Op(Instruction[27:24]));
  Comparator #(.width(3)) comparator_4 (.a(Instruction[31:29]), .b(3'b111), .eq(comparator_4_eq));  // open: gt, lt
  Multiplexer #(.width(32), .enable("false")) multiplexer_2 (
    .in0(PC), .in1(ALU_Result), .out(Memory_Address), .sel(MCLK));
  Transistor #(.\type ("n"), .gate("br"), .width(32)) transistor_1 (
    .in(ALU_Result), .out(Write_Data), .gate(comparator_4_eq));
  buf buffer_1 (Write_Enable, comparator_4_eq);
  Register #(.width(32), .trigger("low")) register_2 (
    .D(Memory_Read), .Q({Instruction, i}), .clk(MCLK));  // open: en, clr
  Register #(.width(32), .trigger("high")) register_3 (.D(Memory_Read), .Q(register_3_q), .clk(MCLK));  // open: en, clr
  and Write (Memory_Write_Enable, Instruction[29], comparator_5_eq);
  and toB (toB_out, ~Instruction[29], comparator_5_eq);  // AND_Gate
  Comparator #(.width(2)) comparator_5 (.a(Instruction[31:30]), .b(2'b10), .eq(comparator_5_eq));  // open: gt, lt
  Comparator #(.width(32)) comparator_6 (.a(B), .b({32{1'b0}}), .gt(comparator_6_gt));  // open: eq, lt
  Transistor #(.\type ("n"), .gate("br"), .width(32)) transistor_2 (
    .in(register_3_q), .out(Write_Data), .gate(toB_out));
  buf buffer_2 (Write_Enable, toB_out);
  Adder #(.width(32)) adder_1 (.a(32'h1), .b(PC), .out(adder_1_out));  // open: cin, cout
  xor \xor  (xor_out, comparator_6_gt, Instruction[29]);
  and BR (BR_out, xor_out, comparator_7_eq);
  Comparator #(.width(2)) comparator_7 (.a(Instruction[31:30]), .b(2'b01), .eq(comparator_7_eq));  // open: gt, lt
  Multiplexer #(.width(32), .enable("false")) multiplexer_3 (
    .in0(adder_1_out), .in1(ALU_Result), .out(Next_PC), .sel(BR_out));
  // AND_Gate and_1 is placed but not wired

  // Other names for the same wires on the sheet: Instruction[15:0] = i; op[7:0] = Instruction[31:24];
  //   Memory_Write[31:0] = B

  // Notes on the sheet:
  //   Von Neumann Memory Space
  //   ROM
  //   RAM
  //   contents of rom_1 (hex, n*v repeats v):
  //   fc210000 9cf80002 fcff0002 1000000 9c200100 ec010000 2100000 ac810000 fc2f0003 247*0 1
  //   buffer_1 drives only 1 and floats otherwise
  //   Memory & Instruction Loading
  //   buffer_2 drives only 1 and floats otherwise
  //   Program Flow
  //   Memory Bus
  //   ~ write on falling
endmodule

// ALU 32
module ALU (
  input  [31:0] A,
  input  [31:0] B,
  input  [3:0] Op,
  output [31:0] R
);

  wire comparator_1_eq, comparator_1_gt, comparator_1_lt, not_2_out;
  wire [4:0] bit_extender_1_out;
  wire [31:0] adder_1_out, and_1_out, bit_extender_2_out, bit_extender_3_out, bit_extender_4_out,
       bit_extender_5_out, divider_1_out, multiplier_1_out, not_1_out, or_1_out, shifter_1_out,
       shifter_2_out, subtractor_1_out, xor_1_out;

  assign not_1_out = ~B;  // NOT_Gate not_1, 32 bits wide
  assign and_1_out = A & B;  // AND_Gate and_1, 32 bits wide
  assign or_1_out = A | B;  // OR_Gate or_1, 32 bits wide
  assign xor_1_out = A ^ B;  // XOR_Gate xor_1, 32 bits wide
  Bit_Extender #(.in_width(32), .out_width(5)) bit_extender_1 (.in(B), .out(bit_extender_1_out));
  Adder #(.width(32)) adder_1 (.a(A), .b(B), .out(adder_1_out));  // open: cin, cout
  Subtractor #(.width(32)) subtractor_1 (.a(A), .b(B), .out(subtractor_1_out));  // open: bin, bout
  Multiplier #(.width(32)) multiplier_1 (.a(A), .b(B), .out(multiplier_1_out));  // open: cin, cout
  Divider #(.width(32)) divider_1 (.a(A), .b(B), .out(divider_1_out));  // open: upper, rem
  Comparator #(.width(32), .mode("unsigned")) comparator_1 (
    .a(A), .b(B), .gt(comparator_1_gt), .eq(comparator_1_eq), .lt(comparator_1_lt));
  not not_2 (not_2_out, comparator_1_eq);
  Shifter #(.width(32)) shifter_1 (.in(A), .\dist (bit_extender_1_out), .out(shifter_1_out));
  Shifter #(.width(32), .shift("lr")) shifter_2 (.in(A), .\dist (bit_extender_1_out), .out(shifter_2_out));
  assign bit_extender_2_out = {{31{1'b0}}, comparator_1_lt};  // Bit_Extender bit_extender_2
  assign bit_extender_3_out = {{31{1'b0}}, comparator_1_gt};  // Bit_Extender bit_extender_3
  assign bit_extender_4_out = {{31{1'b0}}, comparator_1_eq};  // Bit_Extender bit_extender_4
  assign bit_extender_5_out = {{31{1'b0}}, not_2_out};  // Bit_Extender bit_extender_5
  Multiplexer #(.select(4), .width(32), .enable("false")) multiplexer_1 (
    .in0(not_1_out), .in1(and_1_out), .in2(or_1_out), .in3(xor_1_out), .in4(bit_extender_2_out),
    .in5(bit_extender_3_out), .in6(bit_extender_4_out), .in7(bit_extender_5_out), .in8(shifter_1_out),
    .in9(shifter_2_out), .in12(adder_1_out), .in13(subtractor_1_out), .in14(multiplier_1_out),
    .in15(divider_1_out), .out(R), .sel(Op));  // open: in10, in11
endmodule
